# Fritzing sketch 接线 (saved by Fritzing 0.9.3b)

parts:
  Part1 = Arduino Mega 2560 (Rev3)
  J1 = female pin header, 2 pins [form="♀ (female)"]
  J2 = female pin header, 2 pins [form="♀ (female)"]
  J3 = female pin header, 2 pins [form="♀ (female)"]
  J4 = female pin header, 2 pins [form="♀ (female)"]
  J5 = female pin header, 2 pins [form="♀ (female)"]
  J6 = female pin header, 5 pins [form="♀ (female)"]

nets:
  N1: Part1.SCL, J6.pin4
  N2: Part1.SDA, J6.pin3
  N3: Part1.GND, J4.pin1, J6.pin2
  N4: Part1.3V3, J6.pin1
  N5: Part1.D2_PWM, J6.pin5
  N6: Part1.D3_PWM, J4.pin2
  N7: Part1.D4_PWM, J3.pin2
  N8: Part1.D5_PWM, J2.pin2
  N9: Part1.D6_PWM, J1.pin2
  N10: Part1.D7_PWM, J5.pin2
