# Fritzing sketch forAll (saved by Fritzing 0.9.3b)
circuit board: 4.86373cm x 6.57563cm
breadboards: 1

parts:
  SemiAngle = Arduino Nano (Rev3.0)
  s = female pin header, 3 pins [form="♀ (female)"]
  12 = female pin header, 2 pins [form="♀ (female)"]
  11 = female pin header, 2 pins [form="♀ (female)"]
  10 = female pin header, 2 pins [form="♀ (female)"]
  - = female pin header, 2 pins [form="♀ (female)"]
  R1 = Resistor [tolerance=±5% resistance=220 package=THT]
  GND = female pin header, 3 pins [form="♀ (female)"]
  GND1 = female pin header, 3 pins [form="♀ (female)"]
  R3 = Resistor [tolerance=±5% resistance=220 package=THT]
  10_2 = female pin header, 2 pins [form="♀ (female)"]
  10_3 = female pin header, 2 pins [form="♀ (female)"]
  10_4 = female pin header, 2 pins [form="♀ (female)"]
  10_5 = female pin header, 2 pins [form="♀ (female)"]
  R2 = Resistor [tolerance=±5% resistance=220 package=THT]
  + = female pin header, 3 pins [form="♀ (female)"]
  GND2 = female pin header, 3 pins [form="♀ (female)"]
  R4 = Resistor [tolerance=±5% resistance=220 package=THT]
  10_6 = female pin header, 2 pins [form="♀ (female)"]
  OLDE = female pin header, 4 pins [form="♀ (female)"]
  J1 = female pin header, 2 pins [form="♀ (female)"]
  J2 = female pin header, 2 pins [form="♀ (female)"]
  J3 = female pin header, 2 pins [form="♀ (female)"]
  J4 = female pin header, 2 pins [form="♀ (female)"]
  J5 = female pin header, 2 pins [form="♀ (female)"]
  J6 = female pin header, 2 pins [form="♀ (female)"]
  J7 = female pin header, 2 pins [form="♀ (female)"]
  R5 = Resistor [tolerance=±5% resistance=220 package=THT]

nets:
  N1: SemiAngle.GND, s.pin1, 12.pin2, 11.pin2, 10.pin2, -.pin2, R1.Pin_1, GND.pin1, GND1.pin1, R3.Pin_1, 10_2.pin1, 10_3.pin1, 10_4.pin1, 10_5.pin2, R2.Pin_1, +.pin1, GND2.pin1, R4.Pin_1, 10_6.pin2, OLDE.pin1, J1.pin1, J2.pin1, J3.pin1, J4.pin1, J5.pin1, J6.pin1, J7.pin1, R5.Pin_0
  N2: SemiAngle.D2, +.pin2
  N3: SemiAngle.D3, s.pin2, R1.Pin_0
  N4: SemiAngle.D4, GND.pin2, R2.Pin_0
  N5: SemiAngle.D5, GND1.pin2, R3.Pin_0
  N6: SemiAngle.D6, GND2.pin2, R4.Pin_0
  N7: SemiAngle.D7, J7.pin2, R5.Pin_1
  N8: SemiAngle.D8, 10_6.pin1
  N9: SemiAngle.D9, 10_5.pin1
  N10: SemiAngle.D10, 10.pin1
  N11: SemiAngle.D11/MOSI, 11.pin1
  N12: SemiAngle.D12/MISO, 12.pin1
  N13: SemiAngle.VIN, s.pin3, -.pin1, GND.pin3, GND1.pin3, 10_2.pin2, 10_3.pin2, 10_4.pin2, +.pin3, GND2.pin3, OLDE.pin2
  N14: SemiAngle.A5, OLDE.pin3
  N15: SemiAngle.A4, OLDE.pin4
  N16: SemiAngle.A2, J1.pin2
  N17: SemiAngle.A1, J2.pin2
  N18: SemiAngle.A0, J3.pin2
  N19: SemiAngle.AREF, J4.pin2
  N20: SemiAngle.3V3, J5.pin2
  N21: SemiAngle.D13/SCK, J6.pin2
