# Fritzing sketch miniController2 (saved by Fritzing 0.9.3b)
circuit board: 5cm x 5.5cm
breadboards: 1

parts:
  SemiAngle = Arduino Nano (Rev3.0)
  switch1 = female pin header, 3 pins [form="♀ (female)"]
  s = female pin header, 3 pins [form="♀ (female)"]
  + = female pin header, 3 pins [form="♀ (female)"]
  12 = female pin header, 2 pins [form="♀ (female)"]
  11 = female pin header, 2 pins [form="♀ (female)"]
  10 = female pin header, 2 pins [form="♀ (female)"]
  - = female pin header, 2 pins [form="♀ (female)"]
  R1 = Resistor [tolerance=±5% resistance=220 package=THT]
  R2 = Resistor [tolerance=±5% resistance=220 package=THT]
  R3 = Resistor [tolerance=±5% resistance=220 package=THT]
  GND = female pin header, 3 pins [form="♀ (female)"]
  GND1 = female pin header, 3 pins [form="♀ (female)"]
  R4 = Resistor [tolerance=±5% resistance=220 package=THT]
  10_2 = female pin header, 2 pins [form="♀ (female)"]
  10_3 = female pin header, 2 pins [form="♀ (female)"]
  10_4 = female pin header, 2 pins [form="♀ (female)"]

nets:
  N1: SemiAngle.D2, s.pin2, R1.Pin_0
  N2: SemiAngle.D3, +.pin2, R2.Pin_0
  N3: SemiAngle.D4, R3.Pin_0, GND.pin2
  N4: SemiAngle.D5, GND1.pin2, R4.Pin_0
  N5: SemiAngle.D6, switch1.pin1
  N6: SemiAngle.D7, switch1.pin3
  N7: SemiAngle.D10, 10.pin1
  N8: SemiAngle.D11/MOSI, 11.pin1
  N9: SemiAngle.D12/MISO, 12.pin1
  N10: SemiAngle.VIN, s.pin3, +.pin3, -.pin1, GND.pin3, GND1.pin3, 10_2.pin2, 10_3.pin2, 10_4.pin2
  N11: switch1.pin2, s.pin1, +.pin1, 12.pin2, 11.pin2, 10.pin2, -.pin2, R1.Pin_1, R2.Pin_1, R3.Pin_1, GND.pin1, GND1.pin1, R4.Pin_1, 10_2.pin1, 10_3.pin1, 10_4.pin1
