# Fritzing sketch multi_switches (saved by Fritzing 0.9.3b)
circuit board: 4.8344cm x 5.6721cm
breadboards: 1

parts:
  Multi-Switches = Arduino Nano (Rev3.0)
  SemiAngle = Power Jack [package=power_jack_pth_lock]
  J2 = female pin header, 2 pins [form="♀ (female)"]
  Switches_10_1 = female pin header, 2 pins [form="♀ (female)"]
  J4 = female pin header, 2 pins [form="♀ (female)"]
  J5 = female pin header, 2 pins [form="♀ (female)"]
  J6 = female pin header, 2 pins [form="♀ (female)"]
  J8 = female pin header, 2 pins [form="♀ (female)"]
  J9 = female pin header, 2 pins [form="♀ (female)"]
  J10 = female pin header, 2 pins [form="♀ (female)"]
  J11 = female pin header, 2 pins [form="♀ (female)"]
  J12 = female pin header, 2 pins [form="♀ (female)"]
  J13 = female pin header, 2 pins [form="♀ (female)"]
  OLED_GND = female pin header, 4 pins [form="♀ (female)"]
  R1 = Resistor [tolerance=±5% resistance=220 package=THT]
  R2 = Resistor [tolerance=±5% resistance=220 package=THT]
  ESignal2 = female pin header, 2 pins [form="♀ (female)"]
  Esignal1 = female pin header, 2 pins [form="♀ (female)"]

nets:
  N1: Multi-Switches.GND, SemiAngle.PWR, J2.pin2, Switches_10_1.pin2, J4.pin2, J5.pin2, J6.pin2, J8.pin2, J9.pin2, J10.pin2, J11.pin2, J12.pin2, J13.pin1, OLED_GND.pin1, ESignal2.pin1, Esignal1.pin1
  N2: Multi-Switches.D2, J2.pin1
  N3: Multi-Switches.D3, Switches_10_1.pin1
  N4: Multi-Switches.D4, J4.pin1
  N5: Multi-Switches.D5, J5.pin1
  N6: Multi-Switches.D6, J6.pin1
  N7: Multi-Switches.D8, J8.pin1
  N8: Multi-Switches.D9, J9.pin1
  N9: Multi-Switches.D10, J10.pin1
  N10: Multi-Switches.D11/MOSI, J11.pin1
  N11: Multi-Switches.D12/MISO, J12.pin1
  VIN: Multi-Switches.VIN, SemiAngle.GND, OLED_GND.pin2
  N12: Multi-Switches.A5, R1.Pin_0
  N13: Multi-Switches.A4, R2.Pin_0
  N14: Multi-Switches.A2, J13.pin2
  N15: Multi-Switches.A1, Esignal1.pin2
  N16: Multi-Switches.A0, ESignal2.pin2
  N17: OLED_GND.pin3, R1.Pin_1
  N18: OLED_GND.pin4, R2.Pin_1
