# Fritzing sketch masterReader (saved by Fritzing 0.9.3b)
circuit board: 8.91884cm x 5.55901cm
breadboards: 1
perfboards: 1

parts:
  J4 = rounded female pin header, 4 pins [form="♀ (female rounded)"]
  Grove1 = Grove OLED 128x96
  S1 = SWITCH-MOMENTARY-2 [part_number=rst package=tactile-pth]
  J3 = rounded female pin header, 4 pins [form="♀ (female rounded)"]
  J5 = rounded female pin header, 4 pins [form="♀ (female rounded)"]
  J6 = rounded female pin header, 4 pins [form="♀ (female rounded)"]
  J7 = rounded female pin header, 4 pins [form="♀ (female rounded)"]
  J8 = rounded female pin header, 4 pins [form="♀ (female rounded)"]
  J9 = rounded female pin header, 4 pins [form="♀ (female rounded)"]
  J10 = rounded female pin header, 4 pins [form="♀ (female rounded)"]
  J11 = rounded female pin header, 4 pins [form="♀ (female rounded)"]
  J12 = rounded female pin header, 4 pins [form="♀ (female rounded)"]
  J13 = rounded female pin header, 4 pins [form="♀ (female rounded)"]
  Part1 = Arduino Nano (Rev3.0)
  J2 = rounded female pin header, 4 pins [form="♀ (female rounded)"]
  S2 = Toggle Switch [package=THT]
  Power_plug1 = Power plug
  R2 = Resistor [tolerance=±5% resistance=220 package="1206 [SMD]"]
  R1 = Resistor [tolerance=±5% resistance=220 package="1206 [SMD]"]
  R4 = Resistor [tolerance=±5% resistance=220 package="1206 [SMD]"]
  J14 = rounded female pin header, 4 pins [form="♀ (female rounded)"]
  R3 = Resistor [tolerance=±5% resistance=220 package="1206 [SMD]"]
  LED1 = LED - 5mm [color="Red (633nm)" package="5 mm [THT]"]
  R5 = Resistor [tolerance=±5% resistance=220 package="1206 [SMD]"]
  LED2 = LEDs [package=fkit-led-1206]
  J1 = screw terminal, 6 pins  # not connected
  J15 = screw terminal, 6 pins  # not connected
  J16 = screw terminal, 6 pins  # not connected
  J17 = screw terminal, 6 pins  # not connected
  J18 = screw terminal, 6 pins  # not connected
  J19 = screw terminal, 6 pins  # not connected
  J20 = screw terminal, 6 pins  # not connected
  J21 = screw terminal, 6 pins  # not connected
  J22 = screw terminal, 6 pins  # not connected
  J23 = screw terminal, 6 pins  # not connected
  J24 = screw terminal, 6 pins  # not connected
  J25 = screw terminal, 6 pins  # not connected

nets:
  N1: J4.pin1, Grove1.SCL, J3.pin1, J5.pin1, J6.pin1, J7.pin1, J8.pin1, J9.pin1, J10.pin1, J11.pin1, J12.pin1, J13.pin1, Part1.A5, J2.pin1, R3.Pin_1
  N2: J4.pin2, Grove1.SDA, J3.pin2, J5.pin2, J6.pin2, J7.pin2, J8.pin2, J9.pin2, J10.pin2, J11.pin2, J12.pin2, J13.pin2, Part1.A4, J2.pin2, R2.Pin_1
  GND: J4.pin3, Grove1.GND, J3.pin3, J5.pin3, J6.pin3, J7.pin3, J8.pin3, J9.pin3, J10.pin3, J11.pin3, J12.pin3, J13.pin3, Part1.GND, J2.pin3, Power_plug1.GND, R1.Pin_1, R4.Pin_0, J14.pin2, J14.pin3, R5.Pin_0
  N3: J4.pin4, Part1.D4
  VCC: Grove1.VCC, S1.1, Part1.5V, S2.COM, R2.Pin_0, R3.Pin_0
  N4: S1.2, Part1.A1, R1.Pin_0, J14.pin4
  N5: J3.pin4, Part1.D3
  N6: J5.pin4, Part1.D5
  N7: J6.pin4, Part1.D7
  N8: J7.pin4, Part1.D6
  N9: J8.pin4, Part1.D8
  N10: J9.pin4, Part1.D9
  N11: J10.pin4, Part1.D11/MOSI
  N12: J11.pin4, Part1.D10
  N13: J12.pin4, Part1.D12/MISO
  N14: J13.pin4, Part1.D13/SCK
  N15: Part1.D2, J2.pin4
  VIN: Part1.VIN, Power_plug1.VCC
  N16: Part1.A2, S2.L1, R4.Pin_1
  N17: Part1.A0, J14.pin1, LED1.anode, LED2.C
  N18: LED1.cathode, R5.Pin_1, LED2.A

notes:
  SIG GND SDA SCL
  GND
  face down
  RST GND GND OUT
