# Fritzing sketch masterReader2.0 (saved by Fritzing 0.9.3b)
circuit board: 9.05765cm x 7.05733cm
breadboards: 1
perfboards: 1

parts:
  Grove1 = Grove OLED 128x96
  S1 = SWITCH-MOMENTARY-2 [part_number=rst package=tactile-pth]
  Part1 = Arduino Nano (Rev3.0)
  Power_plug1 = Power plug
  J14 = rounded female pin header, 4 pins [form="♀ (female rounded)"]
  J1 = screw terminal, 6 pins
  J15 = screw terminal, 6 pins
  J16 = screw terminal, 6 pins
  J17 = screw terminal, 6 pins
  J18 = screw terminal, 6 pins
  J19 = screw terminal, 6 pins
  J20 = screw terminal, 6 pins
  J21 = screw terminal, 6 pins
  J22 = screw terminal, 6 pins
  J23 = screw terminal, 6 pins
  J24 = screw terminal, 6 pins
  J25 = screw terminal, 6 pins
  Z2 = VARISTOR [package=0603-res]
  LED2 = LEDs [package=led-0603]
  Z4 = VARISTOR [package=0603-res]
  S3 = Tilt Switch [package=THT]
  R3 = Resistor [tolerance=±5% resistance=220 package="0603 [SMD]"]
  R2 = Resistor [tolerance=±5% resistance=220 package="0603 [SMD]"]
  R4 = Resistor [tolerance=±5% resistance=220 package="0603 [SMD]"]
  J26 = screw terminal, 4 pins  # not connected

nets:
  GND: Grove1.GND, Part1.GND, Power_plug1.GND, J14.pin2, J14.pin3, J1.pin3, J1.pin4, J15.pin3, J15.pin4, J16.pin3, J16.pin4, J17.pin3, J17.pin4, J18.pin3, J18.pin4, J19.pin3, J19.pin4, J20.pin3, J20.pin4, J21.pin3, J21.pin4, J22.pin3, J22.pin4, J23.pin3, J23.pin4, J24.pin3, J24.pin4, J25.pin3, J25.pin4, Z2.2, Z4.2, R4.Pin_0
  VCC: Grove1.VCC, S1.1, Part1.5V, J1.pin2, J15.pin2, J16.pin2, J17.pin2, J18.pin2, J19.pin2, J20.pin2, J21.pin2, J22.pin2, J23.pin2, J24.pin2, J25.pin2, S3.Pin_2, R3.Pin_0, R2.Pin_0
  N1: Grove1.SDA, Part1.A5, J1.pin6, J15.pin6, J16.pin6, J17.pin6, J18.pin6, J19.pin6, J20.pin6, J21.pin6, J22.pin6, J23.pin6, J24.pin6, J25.pin6, R2.Pin_1
  N2: Grove1.SCL, Part1.A4, J1.pin5, J15.pin5, J16.pin5, J17.pin5, J18.pin5, J19.pin5, J20.pin5, J21.pin5, J22.pin5, J23.pin5, J24.pin5, J25.pin5, R3.Pin_1
  N3: S1.2, Part1.A1, J14.pin4, Z4.1
  N4: Part1.D2, J19.pin1
  N5: Part1.D3, J20.pin1
  N6: Part1.D4, J22.pin1
  N7: Part1.D5, J25.pin1
  N8: Part1.D6, J23.pin1
  N9: Part1.D7, J24.pin1
  N10: Part1.D8, J1.pin1
  N11: Part1.D9, J15.pin1
  N12: Part1.D10, J17.pin1
  N13: Part1.D11/MOSI, J16.pin1
  N14: Part1.D12/MISO, J18.pin1
  VIN: Part1.VIN, Power_plug1.VCC
  N15: Part1.A2, S3.Pin_1, R4.Pin_1
  N16: Part1.A0, J14.pin1, LED2.A
  N17: Part1.D13/SCK, J21.pin1
  N18: Z2.1, LED2.C

notes:
  GND
  face down
  RST GND GND OUT
  SIG VIN GND GND SDA SCL
