# Fritzing sketch masterReader3_0 (saved by Fritzing 0.9.3b)
circuit board: 8.12075cm x 6.00058cm
breadboards: 1
perfboards: 1

parts:
  p12 = screw terminal, 6 pins
  p11 = screw terminal, 6 pins
  p9 = screw terminal, 6 pins
  p10 = screw terminal, 6 pins
  p8 = screw terminal, 6 pins
  p6 = screw terminal, 6 pins
  p5 = screw terminal, 6 pins
  p7 = screw terminal, 6 pins
  p4 = screw terminal, 6 pins
  p2 = screw terminal, 6 pins
  p1 = screw terminal, 6 pins
  p3 = screw terminal, 6 pins
  screen = screw terminal, 4 pins
  S1 = SWITCH-MOMENTARY-2 [package=tactile-pth]
  J27 = Power Jack [package=power_jack_slot]
  S6 = Toggle Switch [package=THT]
  Part1 = Arduino Nano (Rev3.0)
  R5 = Resistor [tolerance=±5% resistance=220 package="0805 [SMD]"]
  R6 = Resistor [tolerance=±5% resistance=220 package="0805 [SMD]"]
  R7 = Resistor [tolerance=±5% resistance=220 package="0805 [SMD]"]
  R8 = Resistor [tolerance=±5% resistance=220 package="0805 [SMD]"]
  R9 = Resistor [tolerance=±5% resistance=220 package="0805 [SMD]"]
  LED3 = smd LED [color="Red (633nm)" package="0805 [SMD]"]
  J14 = rounded female pin header, 6 pins [form="♀ (female rounded)"]

nets:
  N1: p12.pin1, Part1.D13/SCK
  N2: p12.pin2, p11.pin2, p9.pin2, p10.pin2, p8.pin2, p6.pin2, p5.pin2, p7.pin2, p4.pin2, p2.pin2, p1.pin2, p3.pin2, screen.pin2, S1.1, S6.COM, Part1.5V, R6.Pin_1, R7.Pin_1
  GND: p12.pin3, p12.pin4, p11.pin3, p11.pin4, p9.pin3, p9.pin4, p10.pin3, p10.pin4, p8.pin3, p8.pin4, p6.pin3, p6.pin4, p5.pin3, p5.pin4, p7.pin3, p7.pin4, p4.pin3, p4.pin4, p2.pin3, p2.pin4, p1.pin3, p1.pin4, p3.pin3, p3.pin4, screen.pin1, J27.GND, Part1.GND, R5.Pin_1, R8.Pin_0, R9.Pin_0, J14.pin2, J14.pin3, J14.pin5
  N3: p12.pin5, p11.pin5, p9.pin5, p10.pin5, p8.pin5, p6.pin5, p5.pin5, p7.pin5, p4.pin5, p2.pin5, p1.pin5, p3.pin5, screen.pin4, Part1.A4, R7.Pin_0
  N4: p12.pin6, p11.pin6, p9.pin6, p10.pin6, p8.pin6, p6.pin6, p5.pin6, p7.pin6, p4.pin6, p2.pin6, p1.pin6, p3.pin6, screen.pin3, Part1.A5, R6.Pin_0
  N5: p11.pin1, Part1.D12/MISO
  N6: p9.pin1, Part1.D10
  N7: p10.pin1, Part1.D11/MOSI
  N8: p8.pin1, Part1.D9
  N9: p6.pin1, Part1.D7
  N10: p5.pin1, Part1.D6
  N11: p7.pin1, Part1.D8
  N12: p4.pin1, Part1.D5
  N13: p2.pin1, Part1.D3
  N14: p1.pin1, Part1.D2
  N15: p3.pin1, Part1.D4
  N16: S1.2, Part1.A1, R5.Pin_0, J14.pin4
  N17: J27.PWR, Part1.VIN
  N18: S6.L2, Part1.A2, R8.Pin_1
  N19: Part1.A3, J14.pin6
  N20: Part1.A0, LED3.cathode, J14.pin1
  N21: R9.Pin_1, LED3.anode

notes:
  GND
  NOUT GND RST GND GND OUT
  SIG VIN GND GND SDA SCL
  GND VCC SCL SDA
